# Fritzing sketch room_light_bench (saved by Fritzing 0.9.6b)

parts:
  Arduino_MKR_WiFi_1010 = Arduino MKR WIFI 1010
  Barrel_jack_(5_V_2_A_supply) = Power Jack [package=power_jack_slot]
  Screw_terminal = Camdenboss CTB0158-2 [part_number=CTB0158-2 package=THT]
  1N4007_(band_toward_strip) = Rectifier Diode [part_number=1N4007 package="300 mil [THT]"]
  1000_uF = Electrolytic Capacitor [capacitance=1000µF voltage=6.3V package="200 mil [THT, electrolytic]"]
  330_ohm_data_resistor = Resistor [resistance=330 tolerance=±5% power=0.25W package=THT]
  JST_SM_3-pin_(strip_input) = JST-B3P-VH [part_number=JST-B3P-VH package=THT]
  Adafruit_4689_NeoPixel_RGBW_neon_strip_(stand-in) = WS2815 RGB LED strip

nets:
  GND: Arduino_MKR_WiFi_1010.GND, Screw_terminal.terminal_2, 1000_uF.-, JST_SM_3-pin_(strip_input).pin3, Adafruit_4689_NeoPixel_RGBW_neon_strip_(stand-in).GND
  N1: Arduino_MKR_WiFi_1010.D6, 330_ohm_data_resistor.Pin_0
  N2: Barrel_jack_(5_V_2_A_supply).GND, Screw_terminal.pin2
  N3: Barrel_jack_(5_V_2_A_supply).PWR, Screw_terminal.pin1
  N4: Screw_terminal.terminal_1, 1N4007_(band_toward_strip).anode
  N5: 1N4007_(band_toward_strip).cathode, 1000_uF.+, JST_SM_3-pin_(strip_input).pin1, Adafruit_4689_NeoPixel_RGBW_neon_strip_(stand-in).VCC
  N6: 330_ohm_data_resistor.Pin_1, JST_SM_3-pin_(strip_input).pin2, Adafruit_4689_NeoPixel_RGBW_neon_strip_(stand-in).DIN

custom parts:
  Arduino MKR WIFI 1010: The MKR WIFI 1010 is a significant improvement on the MKR 1000 WIFI. It's equipped with an ESP32 module made by U-BLOX. This board aims to speed up and simplify the prototyping of WiFi based IoT applications thanks to the flexibility of the ESP32 module and its low power consumption. The board is composed of three main blocks: SAMD21 Cortex-M0+ 32bit Low Power ARM MCU; U-BLOX NINA-W10 Series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
